// Logisim project atividade3.circ as structural Verilog: 4 circuits, main circuit main
module main (
  input  VEM_UM,
  input  INVA,
  input  A,
  input  ENA,
  input  B,
  input  ENB,
  input  F0,
  input  F1,
  output Saida,
  output VAI_UM
);

  wire and_1_out, and_2_out, decodificador_1_saida_pra_somador_completo,
       decodificador_1_saida_pra_unidade_logica_1, decodificador_1_saida_pra_unidade_logica_2,
       decodificador_1_saida_pra_unidade_logica_3, somador_completo_1_soma, unidade_logica_1_saida_1_bend,
       unidade_logica_1_saida_1_inva_a_ena, unidade_logica_1_saida_2, unidade_logica_1_saida_2_2,
       unidade_logica_1_saida_2_3, xor_1_out;

  and and_1 (and_1_out, A, ENA);
  and and_2 (and_2_out, B, ENB);
  xor xor_1 (xor_1_out, INVA, and_1_out);
  Decodificador decodificador_1 (
    .F0(F0), .F1(F1), .Saida_pra_unidade_logica_1(decodificador_1_saida_pra_unidade_logica_1),
    .Saida_pra_unidade_logica_2(decodificador_1_saida_pra_unidade_logica_2),
    .Saida_pra_unidade_logica_3(decodificador_1_saida_pra_unidade_logica_3),
    .Saida_pra_somador_completo(decodificador_1_saida_pra_somador_completo));
  Unidade_Logica unidade_logica_1 (
    .Entrada_INVA_A_ENA(xor_1_out), .Entrada_BENB(and_2_out), .Saida_1_BEND(unidade_logica_1_saida_1_bend),
    .Saida_1_INVA_A_ENA(unidade_logica_1_saida_1_inva_a_ena),
    .EntradaD_1(decodificador_1_saida_pra_unidade_logica_1),
    .EntradaD_2(decodificador_1_saida_pra_unidade_logica_2),
    .EntradaD_3(decodificador_1_saida_pra_unidade_logica_3), .Saida_2(unidade_logica_1_saida_2),
    .Saida_2_2(unidade_logica_1_saida_2_2), .Saida_2_3(unidade_logica_1_saida_2_3));
  Somador_completo somador_completo_1 (
    .Entrada_unidade_logica_BENB(unidade_logica_1_saida_1_bend),
    .Entrada_unidade_logica_INVA_A_ENA(unidade_logica_1_saida_1_inva_a_ena),
    .Entrada_decodificador(decodificador_1_saida_pra_somador_completo), .Soma(somador_completo_1_soma),
    .Vem_um(VEM_UM), .Vai_um(VAI_UM));
  or or_1 (Saida, unidade_logica_1_saida_2, unidade_logica_1_saida_2_2, unidade_logica_1_saida_2_3, somador_completo_1_soma);

  // Notes on the sheet:
  //   3.18
endmodule

module Unidade_Logica (
  input  Entrada_INVA_A_ENA,
  input  Entrada_BENB,
  input  EntradaD_1,
  input  EntradaD_2,
  input  EntradaD_3,
  output Saida_2,
  output Saida_2_2,
  output Saida_2_3,
  output Saida_1_BEND,
  output Saida_1_INVA_A_ENA
);

  wire and_1_out, not_1_out, or_1_out;

  not not_1 (not_1_out, Entrada_BENB);
  and and_1 (and_1_out, Entrada_INVA_A_ENA, Entrada_BENB);
  or or_1 (or_1_out, Entrada_INVA_A_ENA, Entrada_BENB);
  and and_2 (Saida_2, and_1_out, EntradaD_1);
  and and_3 (Saida_2_2, or_1_out, EntradaD_2);
  and and_4 (Saida_2_3, not_1_out, EntradaD_3);

  assign Saida_1_BEND = Entrada_INVA_A_ENA;
  assign Saida_1_INVA_A_ENA = Entrada_BENB;
endmodule

module Decodificador (
  input  F0,
  input  F1,
  output Saida_pra_unidade_logica_1,
  output Saida_pra_unidade_logica_2,
  output Saida_pra_unidade_logica_3,
  output Saida_pra_somador_completo
);

  wire not_1_out, not_2_out, not_3_out, not_4_out;

  not not_1 (not_1_out, F0);
  not not_2 (not_2_out, F1);
  not not_3 (not_3_out, F0);
  not not_4 (not_4_out, F1);
  and and_1 (Saida_pra_unidade_logica_1, not_1_out, not_2_out);
  and and_2 (Saida_pra_unidade_logica_2, not_3_out, F1);
  and and_3 (Saida_pra_unidade_logica_3, F0, not_4_out);
  and and_4 (Saida_pra_somador_completo, F0, F1);
endmodule

module Somador_completo (
  input  Vem_um,
  input  Entrada_unidade_logica_BENB,
  input  Entrada_unidade_logica_INVA_A_ENA,
  input  Entrada_decodificador,
  output Soma,
  output Vai_um
);

  wire and_1_out, and_2_out, xor_1_out, xor_2_out;

  and and_1 (and_1_out, Entrada_decodificador, Entrada_unidade_logica_BENB, Entrada_unidade_logica_INVA_A_ENA);
  xor xor_1 (xor_1_out, Entrada_unidade_logica_BENB, Entrada_unidade_logica_INVA_A_ENA);
  and and_2 (and_2_out, Entrada_decodificador, xor_1_out, Vem_um);
  or or_1 (Vai_um, and_1_out, and_2_out);
  xor xor_2 (xor_2_out, Vem_um, xor_1_out);
  and and_3 (Soma, xor_2_out, Entrada_decodificador);
endmodule
